# Fritzing sketch esquema CCL (saved by Fritzing 0.9.2b)

parts:
  Parte1 = Arduino Mega ADK (Rev3)
  MD09B1 = A4988 Stepper Motor Driver Carrier
  M1 = Stepper Motor - Bipolar
  12V = Power plug
  5V = Power plug
  MD09B2 = A4988 Stepper Motor Driver Carrier
  M2 = Stepper Motor - Bipolar
  MD09B3 = A4988 Stepper Motor Driver Carrier
  MD09B4 = A4988 Stepper Motor Driver Carrier
  M3 = Stepper Motor - Bipolar
  M4 = Stepper Motor - Bipolar
  MD09B5 = A4988 Stepper Motor Driver Carrier
  MD09B6 = A4988 Stepper Motor Driver Carrier
  MD09B7 = A4988 Stepper Motor Driver Carrier
  MD09B8 = A4988 Stepper Motor Driver Carrier
  M5 = Stepper Motor - Bipolar
  M6 = Stepper Motor - Bipolar
  M7 = Stepper Motor - Bipolar
  MD09B9 = A4988 Stepper Motor Driver Carrier
  M9 = Stepper Motor - Bipolar
  M8 = Stepper Motor - Bipolar

nets:
  N1: Parte1.D13_PWM, MD09B1.Enable
  N2: Parte1.D10_PWM, MD09B1.STEP
  N3: Parte1.D9_PWM, MD09B2.STEP
  N4: Parte1.D8_PWM, MD09B4.STEP
  N5: Parte1.D2_PWM, MD09B9.STEP
  N6: Parte1.D3_PWM, MD09B7.STEP
  N7: Parte1.D4_PWM, MD09B8.STEP
  N8: Parte1.D5_PWM, MD09B5.STEP
  N9: Parte1.D6_PWM, MD09B6.STEP
  N10: Parte1.D7_PWM, MD09B3.STEP
  N11: MD09B1.RESET, MD09B1.SLEEP
  N12: MD09B1.VMOT, 12V.VCC
  N13: MD09B1.GROUND#141, 12V.GND
  N14: MD09B1.OUT_2B, M1.C
  N15: MD09B1.OUT_2A, M1.A
  N16: MD09B1.OUT_1A, M1.B
  N17: MD09B1.OUT_1B, M1.D
  VDD: MD09B1.VDD, 5V.VCC
  N18: MD09B1.GROUND#147, 5V.GND
  N19: MD09B2.RESET, MD09B2.SLEEP
  N20: MD09B2.OUT_2B, M2.C
  N21: MD09B2.OUT_2A, M2.A
  N22: MD09B2.OUT_1A, M2.B
  N23: MD09B2.OUT_1B, M2.D
  N24: MD09B3.MS3, MD09B3.RESET, MD09B3.SLEEP
  N25: MD09B3.GROUND#141, MD09B3.OUT_2B, M3.C
  N26: MD09B3.OUT_2A, M3.A
  N27: MD09B3.OUT_1A, M3.B
  N28: MD09B3.OUT_1B, M3.D
  N29: MD09B4.MS3, MD09B4.RESET, MD09B4.SLEEP
  N30: MD09B4.OUT_2B, M4.C
  N31: MD09B4.OUT_2A, M4.A
  N32: MD09B4.OUT_1A, M4.B
  N33: MD09B4.OUT_1B, M4.D
  N34: MD09B5.RESET, MD09B5.SLEEP
  N35: MD09B5.OUT_2B, M5.C
  N36: MD09B5.OUT_2A, M5.A
  N37: MD09B5.OUT_1A, M5.B
  N38: MD09B5.OUT_1B, M5.D
  N39: MD09B6.RESET, MD09B6.SLEEP
  N40: MD09B6.OUT_2B, M7.C
  N41: MD09B6.OUT_2A, M7.A
  N42: MD09B6.OUT_1A, M7.B
  N43: MD09B6.OUT_1B, M7.D
  N44: MD09B7.MS3, MD09B7.RESET, MD09B7.SLEEP
  N45: MD09B7.OUT_2B, M8.C
  N46: MD09B7.OUT_2A, M8.A
  N47: MD09B7.OUT_1A, M8.B
  N48: MD09B7.OUT_1B, M8.D
  N49: MD09B8.MS3, MD09B8.RESET, MD09B8.SLEEP
  N50: MD09B8.OUT_2B, M6.C
  N51: MD09B8.OUT_2A, M6.A
  N52: MD09B8.OUT_1A, M6.B
  N53: MD09B8.OUT_1B, M6.D
  N54: MD09B9.MS3, MD09B9.RESET, MD09B9.SLEEP
  N55: MD09B9.OUT_2B, M9.C
  N56: MD09B9.OUT_2A, M9.A
  N57: MD09B9.OUT_1A, M9.B
  N58: MD09B9.OUT_1B, M9.D
