# Fritzing sketch esquema CCL2 (saved by Fritzing 0.9.2b)

parts:
  Parte1 = Arduino Mega ADK (Rev3)
  MD09B1 = A4988 Stepper Motor Driver Carrier
  M_T = Stepper Motor - Bipolar
  12V = Power plug
  5V = Power plug
  MD09B2 = A4988 Stepper Motor Driver Carrier
  M_U = Stepper Motor - Bipolar
  MD09B3 = A4988 Stepper Motor Driver Carrier
  MD09B4 = A4988 Stepper Motor Driver Carrier
  M_V2 = Stepper Motor - Bipolar
  M_V1 = Stepper Motor - Bipolar
  MD09B5 = A4988 Stepper Motor Driver Carrier
  MD09B6 = A4988 Stepper Motor Driver Carrier
  MD09B7 = A4988 Stepper Motor Driver Carrier
  MD09B8 = A4988 Stepper Motor Driver Carrier
  M_X = Stepper Motor - Bipolar
  M_Y1 = Stepper Motor - Bipolar
  M_W = Stepper Motor - Bipolar
  MD09B9 = A4988 Stepper Motor Driver Carrier
  M_Z = Stepper Motor - Bipolar
  M_Y2 = Stepper Motor - Bipolar
  FC_U = SWITCH_SPDT [package=kps-1290]
  FC_V = SWITCH_SPDT [package=kps-1290]
  FC_W = SWITCH_SPDT [package=kps-1290]
  FC_X = SWITCH_SPDT [package=kps-1290]
  FC_Y = SWITCH_SPDT [package=kps-1290]
  FC_Z = SWITCH_SPDT [package=kps-1290]
  FC_T = SWITCH_SPDT [package=kps-1290]
  C1 = Electrolytic Capacitor [capacitance=100µF voltage=16V package="100 mil [THT, electrolytic]"]
  C2 = Electrolytic Capacitor [capacitance=100µF voltage=16V package="100 mil [THT, electrolytic]"]
  C3 = Electrolytic Capacitor [capacitance=100µF voltage=16V package="100 mil [THT, electrolytic]"]
  C4 = Electrolytic Capacitor [capacitance=100µF voltage=16V package="100 mil [THT, electrolytic]"]
  C5 = Electrolytic Capacitor [capacitance=100µF voltage=16V package="100 mil [THT, electrolytic]"]
  C6 = Electrolytic Capacitor [capacitance=100µF voltage=16V package="100 mil [THT, electrolytic]"]
  C7 = Electrolytic Capacitor [capacitance=100µF voltage=16V package="100 mil [THT, electrolytic]"]
  C8 = Electrolytic Capacitor [capacitance=100µF voltage=16V package="100 mil [THT, electrolytic]"]
  C9 = Electrolytic Capacitor [capacitance=100µF voltage=16V package="100 mil [THT, electrolytic]"]

nets:
  GND: Parte1.GND, 5V.GND
  N1: Parte1.D13_PWM, MD09B1.Enable
  N2: Parte1.D8_PWM, MD09B1.STEP
  VIN: Parte1.VIN, MD09B1.VDD, 5V.VCC
  N3: Parte1.D2_PWM, MD09B9.STEP
  N4: Parte1.D3_PWM, MD09B8.STEP
  N5: Parte1.D4_PWM, MD09B5.STEP
  N6: Parte1.D5_PWM, MD09B6.STEP
  N7: Parte1.D6_PWM, MD09B3.STEP, MD09B4.STEP
  N8: Parte1.D7_PWM, MD09B2.STEP
  N9: Parte1.D23, MD09B1.DIR
  N10: Parte1.D25, MD09B2.DIR
  N11: Parte1.D27, MD09B3.DIR, MD09B4.DIR
  N12: Parte1.D29, MD09B6.DIR
  N13: Parte1.D31, MD09B5.DIR
  N14: Parte1.D33, MD09B7.DIR, MD09B8.DIR
  N15: Parte1.D35, MD09B9.DIR
  N16: Parte1.D37, FC_Z.S
  N17: Parte1.D39, FC_Y.S
  N18: Parte1.D41, FC_X.S
  N19: Parte1.D43, FC_W.S
  N20: Parte1.D45, FC_V.S
  N21: Parte1.D47, FC_U.S
  N22: Parte1.D49, FC_T.S
  N23: MD09B1.RESET, MD09B1.SLEEP
  N24: MD09B1.VMOT, 12V.VCC, C1.+
  N25: MD09B1.GROUND#141, 12V.GND, C1.-
  N26: MD09B1.OUT_2B, M_T.C
  N27: MD09B1.OUT_2A, M_T.A
  N28: MD09B1.OUT_1A, M_T.B
  N29: MD09B1.OUT_1B, M_T.D
  N30: MD09B2.RESET, MD09B2.SLEEP
  N31: MD09B2.VMOT, C2.+
  N32: MD09B2.GROUND#141, C2.-
  N33: MD09B2.OUT_2B, M_U.C
  N34: MD09B2.OUT_2A, M_U.A
  N35: MD09B2.OUT_1A, M_U.B
  N36: MD09B2.OUT_1B, M_U.D
  N37: MD09B3.MS3, MD09B3.RESET, MD09B3.SLEEP
  N38: MD09B3.VMOT, C4.+
  N39: MD09B3.GROUND#141, MD09B3.OUT_2B, M_V2.C, C4.-
  N40: MD09B3.OUT_2A, M_V2.A
  N41: MD09B3.OUT_1A, M_V2.B
  N42: MD09B3.OUT_1B, M_V2.D
  N43: MD09B4.MS3, MD09B4.RESET, MD09B4.SLEEP
  N44: MD09B4.VMOT, C3.+
  N45: MD09B4.GROUND#141, C3.-
  N46: MD09B4.OUT_2B, M_V1.C
  N47: MD09B4.OUT_2A, M_V1.A
  N48: MD09B4.OUT_1A, M_V1.B
  N49: MD09B4.OUT_1B, M_V1.D
  N50: MD09B5.RESET, MD09B5.SLEEP
  N51: MD09B5.VMOT, C6.+
  N52: MD09B5.GROUND#141, C6.-
  N53: MD09B5.OUT_2B, M_X.C
  N54: MD09B5.OUT_2A, M_X.A
  N55: MD09B5.OUT_1A, M_X.B
  N56: MD09B5.OUT_1B, M_X.D
  N57: MD09B6.RESET, MD09B6.SLEEP
  N58: MD09B6.VMOT, C5.+
  N59: MD09B6.GROUND#141, C5.-
  N60: MD09B6.OUT_2B, M_W.C
  N61: MD09B6.OUT_2A, M_W.A
  N62: MD09B6.OUT_1A, M_W.B
  N63: MD09B6.OUT_1B, M_W.D
  N64: MD09B7.MS3, MD09B7.RESET, MD09B7.SLEEP
  N65: MD09B7.VMOT, C8.+
  N66: MD09B7.GROUND#141, C8.-
  N67: MD09B7.OUT_2B, M_Y2.C
  N68: MD09B7.OUT_2A, M_Y2.A
  N69: MD09B7.OUT_1A, M_Y2.B
  N70: MD09B7.OUT_1B, M_Y2.D
  N71: MD09B8.MS3, MD09B8.RESET, MD09B8.SLEEP
  N72: MD09B8.VMOT, C7.+
  N73: MD09B8.GROUND#141, C7.-
  N74: MD09B8.OUT_2B, M_Y1.C
  N75: MD09B8.OUT_2A, M_Y1.A
  N76: MD09B8.OUT_1A, M_Y1.B
  N77: MD09B8.OUT_1B, M_Y1.D
  N78: MD09B9.MS3, MD09B9.RESET, MD09B9.SLEEP
  N79: MD09B9.VMOT, C9.+
  N80: MD09B9.GROUND#141, C9.-
  N81: MD09B9.OUT_2B, M_Z.C
  N82: MD09B9.OUT_2A, M_Z.A
  N83: MD09B9.OUT_1A, M_Z.B
  N84: MD09B9.OUT_1B, M_Z.D
