# Fritzing sketch placa drivers (saved by Fritzing 0.9.2b)
perfboards: 2

parts:
  MD09B1 = A4988 Stepper Motor Driver Carrier  # not connected
  C1 = Electrolytic Capacitor [capacitance=100µF voltage=16V package="100 mil [THT, electrolytic]"]  # not connected
  12V = Power plug  # not connected
  MD09B3 = A4988 Stepper Motor Driver Carrier  # not connected
  C3 = Electrolytic Capacitor [capacitance=100µF voltage=16V package="100 mil [THT, electrolytic]"]  # not connected
  MD09B4 = A4988 Stepper Motor Driver Carrier
  C4 = Electrolytic Capacitor [capacitance=100µF voltage=16V package="100 mil [THT, electrolytic]"]  # not connected
  MD09B5 = A4988 Stepper Motor Driver Carrier
  C5 = Electrolytic Capacitor [capacitance=100µF voltage=16V package="100 mil [THT, electrolytic]"]  # not connected
  J25 = female pin header, 1 pin [form="♀ (female)"]
  MD09B6 = A4988 Stepper Motor Driver Carrier
  C6 = Electrolytic Capacitor [capacitance=100µF voltage=16V package="100 mil [THT, electrolytic]"]  # not connected
  MD09B7 = A4988 Stepper Motor Driver Carrier
  MD09B9 = A4988 Stepper Motor Driver Carrier
  MD09B10 = A4988 Stepper Motor Driver Carrier
  MD09B11 = A4988 Stepper Motor Driver Carrier
  C7 = Electrolytic Capacitor [capacitance=100µF voltage=16V package="100 mil [THT, electrolytic]"]  # not connected
  C8 = Electrolytic Capacitor [capacitance=100µF voltage=16V package="100 mil [THT, electrolytic]"]  # not connected
  C9 = Electrolytic Capacitor [capacitance=100µF voltage=16V package="100 mil [THT, electrolytic]"]  # not connected
  C11 = Electrolytic Capacitor [capacitance=100µF voltage=16V package="100 mil [THT, electrolytic]"]  # not connected
  J47 = female pin header, 1 pin [form="♀ (female)"]
  J48 = female pin header, 1 pin [form="♀ (female)"]
  J49 = female pin header, 1 pin [form="♀ (female)"]
  J52 = female pin header, 1 pin [form="♀ (female)"]
  J53 = female pin header, 1 pin [form="♀ (female)"]
  J55 = female pin header, 1 pin [form="♀ (female)"]
  J56 = female pin header, 1 pin [form="♀ (female)"]
  J38 = female pin header, 1 pin [form="♀ (female)"]  # not connected
  J36 = male pin header, 4 pins [form="♂ (male)"]  # not connected
  J32 = male pin header, 4 pins [form="♂ (male)"]  # not connected
  J34 = male pin header, 4 pins [form="♂ (male)"]  # not connected
  J33 = male pin header, 4 pins [form="♂ (male)"]  # not connected
  J51 = male pin header, 1 pin [form="♂ (male)"]
  J58 = male pin header, 1 pin [form="♂ (male)"]
  J43 = male pin header, 2 pins [form="♂ (male)"]  # not connected
  J40 = male pin header, 1 pin [form="♂ (male)"]  # not connected
  J42 = male pin header, 2 pins [form="♂ (male)"]  # not connected
  J37 = male pin header, 1 pin [form="♂ (male)"]  # not connected
  J46 = male pin header, 2 pins [form="♂ (male)"]  # not connected
  J41 = male pin header, 1 pin [form="♂ (male)"]  # not connected
  J44 = male pin header, 2 pins [form="♂ (male)"]  # not connected
  J3 = male pin header, 1 pin [form="♂ (male)"]  # not connected
  J4 = male pin header, 2 pins [form="♂ (male)"]  # not connected
  J13 = male pin header, 1 pin [form="♂ (male)"]  # not connected
  J14 = male pin header, 2 pins [form="♂ (male)"]  # not connected
  J18 = male pin header, 1 pin [form="♂ (male)"]  # not connected
  J19 = male pin header, 2 pins [form="♂ (male)"]  # not connected
  J23 = male pin header, 1 pin [form="♂ (male)"]  # not connected
  J24 = male pin header, 2 pins [form="♂ (male)"]  # not connected
  J28 = male pin header, 1 pin [form="♂ (male)"]  # not connected
  J29 = male pin header, 2 pins [form="♂ (male)"]  # not connected
  J1 = male pin header, 4 pins [form="♂ (male)"]  # not connected
  J12 = male pin header, 4 pins [form="♂ (male)"]  # not connected
  J17 = male pin header, 4 pins [form="♂ (male)"]  # not connected
  J22 = male pin header, 4 pins [form="♂ (male)"]  # not connected
  J27 = male pin header, 4 pins [form="♂ (male)"]  # not connected
  J31 = male pin header, 1 pin [form="♂ (male)"]
  J5 = male pin header, 1 pin [form="♂ (male)"]  # not connected
  J57 = male pin header, 1 pin [form="♂ (male)"]
  J6 = male pin header, 1 pin [form="♂ (male)"]  # not connected
  J15 = male pin header, 1 pin [form="♂ (male)"]  # not connected
  J16 = male pin header, 1 pin [form="♂ (male)"]  # not connected
  J20 = male pin header, 1 pin [form="♂ (male)"]
  J21 = double row male pin header, 2 pins [form="♂ (male)"]
  J26 = male pin header, 1 pin [form="♂ (male)"]
  J30 = male pin header, 1 pin [form="♂ (male)"]

nets:
  N1: MD09B4.RESET, MD09B4.SLEEP
  N2: MD09B4.VMOT, J20.pin1
  N3: MD09B4.GROUND, J21.pin1
  N4: MD09B5.RESET, MD09B5.SLEEP
  N5: MD09B5.VMOT, J25.pin1
  N6: MD09B5.GROUND#141, J26.pin1
  N7: MD09B6.RESET, MD09B6.SLEEP
  N8: MD09B6.VMOT, J30.pin1
  N9: MD09B6.GROUND#141, J31.pin1
  N10: MD09B6.VDD, J57.pin1
  N11: MD09B7.RESET, MD09B7.SLEEP
  N12: MD09B7.VMOT, J47.pin1
  N13: MD09B7.GROUND#141, J52.pin1
  N14: MD09B9.RESET, MD09B9.SLEEP
  N15: MD09B9.VMOT, J48.pin1
  N16: MD09B9.GROUND#141, J53.pin1
  N17: MD09B9.VDD, J58.pin1
  N18: MD09B10.RESET, MD09B10.SLEEP
  N19: MD09B10.VMOT, J49.pin1
  N20: MD09B10.GROUND#141, J55.pin1
  N21: MD09B11.RESET, MD09B11.SLEEP
  N22: MD09B11.VMOT, J51.pin1
  N23: MD09B11.GROUND, J56.pin1
